// Logisim project reptile-8.circ as structural Verilog
module ALU_1 (
  input  op1,
  input  op2,
  input  cin,
  input  [2:0] s,
  output cout,
  output out
);

  wire and_1_out, and_2_out, and_3_out, not_1_out, or_1_out, xor_1_out, xor_2_out, xor_3_out;

  xor xor_1 (xor_1_out, op1, op2);
  and and_1 (and_1_out, xor_1_out, cin);
  and and_2 (and_2_out, op2, op1);
  and and_3 (and_3_out, op1, op2);
  or or_1 (or_1_out, op1, op2);
  not not_1 (not_1_out, op1);
  xor xor_2 (xor_2_out, xor_1_out, cin);
  xor xor_3 (xor_3_out, op1, op2);
  or or_2 (cout, and_1_out, and_2_out);
  Multiplexer #(.select(3), .enable("false")) multiplexer_1 (
    .in0(xor_2_out), .in1(and_3_out), .in2(or_1_out), .in3(xor_3_out), .in4(not_1_out), .in5(op1), .out(out),
    .sel(s));  // open: in6, in7
endmodule

module ALU (
  input  [15:0] op1,
  input  [15:0] op2,
  input  [3:0] s,
  output [15:0] out,
  output z
);

  wire alu_1_1_cout, alu_1_2_cout, alu_1_3_cout, alu_1_4_cout, alu_1_5_cout, alu_1_6_cout, alu_1_7_cout,
       alu_1_8_cout, alu_1_9_cout, alu_1_10_cout, alu_1_11_cout, alu_1_12_cout, alu_1_13_cout, alu_1_14_cout,
       alu_1_15_cout, and_1_out, and_2_out, and_3_out, and_4_out, and_5_out, and_6_out, and_7_out, and_8_out,
       and_9_out, and_10_out, not_1_out, not_2_out, not_3_out, not_4_out, not_5_out, not_6_out, not_7_out,
       not_8_out, not_9_out, not_10_out, not_11_out, not_12_out, not_13_out;
  wire [1:0] or_5_out;
  wire [2:0] or_1_out;
  wire [15:0] multiplexer_1_out, not_14_out;

  not not_1 (not_1_out, s[0]);
  not not_2 (not_2_out, s[1]);
  not not_3 (not_3_out, s[0]);
  not not_4 (not_4_out, s[3]);
  not not_5 (not_5_out, s[3]);
  not not_6 (not_6_out, s[1]);
  not not_7 (not_7_out, s[2]);
  not not_8 (not_8_out, s[0]);
  not not_9 (not_9_out, s[2]);
  not not_10 (not_10_out, s[1]);
  not not_11 (not_11_out, s[2]);
  not not_12 (not_12_out, s[3]);
  not not_13 (not_13_out, s[2]);
  and and_1 (and_1_out, ~s[3], ~s[2], ~s[1], s[0]);  // AND_Gate
  and and_2 (and_2_out, not_1_out, not_2_out, s[3]);
  and and_3 (and_3_out, not_3_out, s[1], not_4_out);
  and and_4 (and_4_out, s[0], s[1], not_5_out);
  and and_5 (and_5_out, not_6_out, s[3]);
  and and_6 (and_6_out, s[0], s[2]);
  and and_7 (and_7_out, s[3], s[1], not_7_out, not_8_out);
  and and_8 (and_8_out, s[3], s[1], s[0], not_9_out);
  and and_9 (and_9_out, s[0], not_10_out, not_11_out, not_12_out);
  and and_10 (and_10_out, s[0], s[1], s[3], not_13_out);
  or or_1 (or_1_out[0], and_2_out, s[2], and_3_out);
  or or_2 (or_1_out[1], s[2], and_4_out);
  or or_3 (or_1_out[2], and_5_out, and_6_out);
  or or_4 (or_5_out[1], and_7_out, and_8_out);
  or or_5 (or_5_out[0], and_9_out, and_10_out);
  assign not_14_out = ~op2;  // NOT_Gate not_14, 16 bits wide
  Multiplexer #(.select(2), .width(16), .enable("false")) multiplexer_1 (
    .in0(op2), .in1(not_14_out), .in2(16'h1), .in3({16{1'b1}}), .out(multiplexer_1_out), .sel(or_5_out));
  ALU_1 alu_1_1 (
    .op1(op1[0]), .op2(multiplexer_1_out[0]), .cin(and_1_out), .cout(alu_1_1_cout), .out(out[0]), .s(or_1_out));
  ALU_1 alu_1_2 (
    .op1(op1[1]), .op2(multiplexer_1_out[1]), .cin(alu_1_1_cout), .cout(alu_1_2_cout), .out(out[1]),
    .s(or_1_out));
  ALU_1 alu_1_3 (
    .op1(op1[2]), .op2(multiplexer_1_out[2]), .cin(alu_1_2_cout), .cout(alu_1_3_cout), .out(out[2]),
    .s(or_1_out));
  ALU_1 alu_1_4 (
    .op1(op1[3]), .op2(multiplexer_1_out[3]), .cin(alu_1_3_cout), .cout(alu_1_4_cout), .out(out[3]),
    .s(or_1_out));
  ALU_1 alu_1_5 (
    .op1(op1[4]), .op2(multiplexer_1_out[4]), .cin(alu_1_4_cout), .cout(alu_1_5_cout), .out(out[4]),
    .s(or_1_out));
  ALU_1 alu_1_6 (
    .op1(op1[5]), .op2(multiplexer_1_out[5]), .cin(alu_1_5_cout), .cout(alu_1_6_cout), .out(out[5]),
    .s(or_1_out));
  ALU_1 alu_1_7 (
    .op1(op1[6]), .op2(multiplexer_1_out[6]), .cin(alu_1_6_cout), .cout(alu_1_7_cout), .out(out[6]),
    .s(or_1_out));
  ALU_1 alu_1_8 (
    .op1(op1[7]), .op2(multiplexer_1_out[7]), .cin(alu_1_7_cout), .cout(alu_1_8_cout), .out(out[7]),
    .s(or_1_out));
  ALU_1 alu_1_9 (
    .op1(op1[8]), .op2(multiplexer_1_out[8]), .cin(alu_1_8_cout), .cout(alu_1_9_cout), .out(out[8]),
    .s(or_1_out));
  ALU_1 alu_1_10 (
    .op1(op1[9]), .op2(multiplexer_1_out[9]), .cin(alu_1_9_cout), .cout(alu_1_10_cout), .out(out[9]),
    .s(or_1_out));
  ALU_1 alu_1_11 (
    .op1(op1[10]), .op2(multiplexer_1_out[10]), .cin(alu_1_10_cout), .cout(alu_1_11_cout), .out(out[10]),
    .s(or_1_out));
  ALU_1 alu_1_12 (
    .op1(op1[11]), .op2(multiplexer_1_out[11]), .cin(alu_1_11_cout), .cout(alu_1_12_cout), .out(out[11]),
    .s(or_1_out));
  ALU_1 alu_1_13 (
    .op1(op1[12]), .op2(multiplexer_1_out[12]), .cin(alu_1_12_cout), .cout(alu_1_13_cout), .out(out[12]),
    .s(or_1_out));
  ALU_1 alu_1_14 (
    .op1(op1[13]), .op2(multiplexer_1_out[13]), .cin(alu_1_13_cout), .cout(alu_1_14_cout), .out(out[13]),
    .s(or_1_out));
  ALU_1 alu_1_15 (
    .op1(op1[14]), .op2(multiplexer_1_out[14]), .cin(alu_1_14_cout), .cout(alu_1_15_cout), .out(out[14]),
    .s(or_1_out));
  ALU_1 alu_1_16 (
    .op1(op1[15]), .op2(multiplexer_1_out[15]), .cin(alu_1_15_cout), .out(out[15]), .s(or_1_out));  // open: cout
  Comparator #(.width(16), .mode("unsigned")) comparator_1 (.a(out), .b({16{1'b0}}), .eq(z));  // open: gt, lt
endmodule

module PC (
  input  [11:0] ld,
  input  PCINC,
  input  PCLD,
  input  clk,
  output [11:0] out_5
);

  wire or_1_out;
  wire [11:0] adder_1_out, multiplexer_1_out;

  Multiplexer #(.width(12), .enable("false")) multiplexer_1 (
    .in0(ld), .in1(adder_1_out), .out(multiplexer_1_out), .sel(PCINC));
  Register #(.width(12)) register_1 (.D(multiplexer_1_out), .en(or_1_out), .Q(out_5), .clk(clk));  // open: clr
  or or_1 (or_1_out, PCINC, PCLD);
  Adder #(.width(12)) adder_1 (.a(12'h1), .b(out_5), .out(adder_1_out));  // open: cin, cout
endmodule

module Regfile (
  input  [2:0] sw,
  input  REGLD,
  input  [15:0] ld,
  input  clk,
  input  [2:0] sr1,
  input  [2:0] sr2,
  output [15:0] R0,
  output [15:0] R1,
  output [15:0] R2
);

  wire and_1_out, and_2_out, and_3_out, and_4_out, and_5_out, and_6_out, and_7_out, and_8_out,
       decoder_1_out0, decoder_1_out1, decoder_1_out2, decoder_1_out3, decoder_1_out4, decoder_1_out5,
       decoder_1_out6, decoder_1_out7;
  wire [15:0] register_1_q, register_2_q, register_3_q, register_4_q, register_5_q, register_6_q,
       register_7_q;

  and and_1 (and_1_out, REGLD, decoder_1_out7);
  and and_2 (and_2_out, REGLD, decoder_1_out6);
  Register #(.width(16)) register_1 (.D(ld), .en(and_1_out), .Q(register_1_q), .clk(clk));  // open: clr
  Multiplexer #(.select(3), .width(16), .enable("false")) multiplexer_1 (
    .in0(R0), .in1(register_7_q), .in2(register_6_q), .in3(register_5_q), .in4(register_4_q),
    .in5(register_3_q), .in6(register_2_q), .in7(register_1_q), .out(R1), .sel(sr1));
  and and_3 (and_3_out, REGLD, decoder_1_out5);
  Register #(.width(16)) register_2 (.D(ld), .en(and_2_out), .Q(register_2_q), .clk(clk));  // open: clr
  Decoder #(.select(3), .enable("false")) decoder_1 (
    .out0(decoder_1_out0), .out1(decoder_1_out1), .out2(decoder_1_out2), .out3(decoder_1_out3),
    .out4(decoder_1_out4), .out5(decoder_1_out5), .out6(decoder_1_out6), .out7(decoder_1_out7), .sel(sw));
  and and_4 (and_4_out, REGLD, decoder_1_out4);
  Register #(.width(16)) register_3 (.D(ld), .en(and_3_out), .Q(register_3_q), .clk(clk));  // open: clr
  Register #(.width(16)) register_4 (.D(ld), .en(and_4_out), .Q(register_4_q), .clk(clk));  // open: clr
  and and_5 (and_5_out, decoder_1_out3, REGLD);
  Register #(.width(16)) register_5 (.D(ld), .en(and_5_out), .Q(register_5_q), .clk(clk));  // open: clr
  and and_6 (and_6_out, decoder_1_out1, REGLD);
  and and_7 (and_7_out, decoder_1_out2, REGLD);
  Register #(.width(16)) register_6 (.D(ld), .en(and_7_out), .Q(register_6_q), .clk(clk));  // open: clr
  and and_8 (and_8_out, decoder_1_out0, REGLD);
  Register #(.width(16)) register_7 (.D(ld), .en(and_6_out), .Q(register_7_q), .clk(clk));  // open: clr
  Register #(.width(16)) register_8 (.D(ld), .en(and_8_out), .Q(R0), .clk(clk));  // open: clr
  Multiplexer #(.select(3), .width(16), .enable("false")) multiplexer_2 (
    .in0(R0), .in1(register_7_q), .in2(register_6_q), .in3(register_5_q), .in4(register_4_q),
    .in5(register_3_q), .in6(register_2_q), .in7(register_1_q), .out(R2), .sel(sr2));
endmodule
